# Fritzing sketch chess (saved by Fritzing 0.9.4)
breadboards: 1

parts:
  IC1 = MCP23017 I2C I/O Expander
  U1 = XIAO ESP32C6 [part_number=" XIAO ESP32C6"]
  Part1 = NeoPixel Stick [part_number=1426]
  S1 = SWITCH-MOMENTARY-2 [package=tactile-pth-12mm]  # not connected
  SW1 = DIP SWITCH [package=dipswitch-02]
  SW2 = DIP SWITCH [package=dipswitch-02]

nets:
  VDD: IC1.VDD, U1.5V, Part1.+5V
  GND: IC1.VSS, U1.GND, Part1.GND
  N1: IC1.SCL, U1.D5
  N2: IC1.SDA, U1.D4
  N3: IC1.A0, SW2.3
  N4: IC1.A1, SW1.4
  N5: IC1.A2, SW1.3
  N6: U1.D7, Part1.DATAIN

custom parts:
  MCP23017 I2C I/O Expander: The MCP23017 uses two i2c pins (these can be shared with other i2c devices), and in exchange gives you 16 general purpose pins. You can set each of 16 pins to be input, output, input with a pullup or open drain. There's even the ability to get an interrupt via an external pin when any of the inputs change so you don't have to keep polling the chip.
  XIAO ESP32C6: XIAO ESP32C6 is a cost-effective MCU based on Espressif’s ESP32-C6. This compact MCU excels in Matter-compliant smart home applications with its support for various wireless connectivity (2.4GHz Wi-Fi 6, BLE 5.0, Zigbee, and Thread). Designed with the thumb-size footprint and a single-sided mount of the XIAO Series, it's perfect for space-limited projects. Encrypted on the chip, the XIAO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
  NeoPixel Stick: Make your own little LED strip arrangement with this stick of NeoPixel LEDs. We crammed 8 of the tiny 5050 (5mm x 5mm) smart RGB LEDs onto a PCB with mounting holes and a chainable design. Use only one microcontroller pin to control as many as you can chain together! Each LED is addressable as the driver chip is inside the LED. Each one has ~18mA constant current drive so the color will be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
